# Fritzing sketch Bike_Alarm (saved by Fritzing 0.9.6b)
circuit board: 15cm x 20cm

parts:
  R6 = Resistor [tolerance=±5% power=0.25 resistance=100 package=THT]
  LED2 = LED - 5mm [color="Blue (430nm)" current=0.030 package="5 mm [THT]"]
  LED5 = LED - 5mm [color="Red (633nm)" current=0.030 package="5 mm [THT]"]
  IR1 = TSOP312.., 314.. [package=THT]
  R1 = Resistor [tolerance=±5% power=0.25 resistance=220 package=THT]
  R3 = Resistor [tolerance=±5% power=0.25 resistance=220 package=THT]
  R2 = Resistor [tolerance=±5% power=0.25 resistance=220 package=THT]
  ATMega328 = atmega328 [package=dip]
  SPKR1 = Loudspeaker
  LED4 = LED - 5mm [color="Blue (430nm)" current=0.030 package="5 mm [THT]"]
  U1 = Voltage Regulator - 5V [package="TO220 [THT]"]
  J2 = Screw terminal - 2 pins [package=THT]
  LED3 = LED - 5mm [color="Red (633nm)" current=0.030 package="5 mm [THT]"]
  R4 = Resistor [tolerance=±5% power=0.25 resistance=220 package=THT]
  R5 = Resistor [tolerance=±5% power=0.25 resistance=220 package=THT]
  HC-SR04_Sensor_1 = HC-SR04 Ultrasonic Distance Sensor
  LED6 = LED - 5mm [color="Red (633nm)" current=30mA package="5 mm [THT]"]
  LED7 = LED - 5mm [color="Blue (430nm)" current=0.030 package="5 mm [THT]"]
  LED8 = LED - 5mm [color="Blue (430nm)" current=0.030 package="5 mm [THT]"]
  R7 = Resistor [tolerance=±5% power=0.25 resistance=220 package=THT]
  LED9 = LED - 5mm [color="Red (633nm)" current=30mA package="5 mm [THT]"]
  LED10 = LED - 5mm [color="Blue (430nm)" current=0.030 package="5 mm [THT]"]
  R8 = Resistor [tolerance=±5% power=0.25 resistance=220 package=THT]
  LED1 = LED - 5mm [color="Red (633nm)" current=30mA package="5 mm [THT]"]
  R9 = Resistor [tolerance=±2% power=0.25 resistance=220 package=THT]
  R11 = Resistor [tolerance=±2% power=0.25 resistance=68 package=THT]

nets:
  N1: R6.Pin_0, SPKR1.pin1
  N2: R6.Pin_1, IR1.GND, R1.Pin_0, R3.Pin_0, R2.Pin_0, ATMega328.GND#7, R4.Pin_0, R5.Pin_0, R7.Pin_0, R8.Pin_0, R9.Pin_0, R11.Pin_0
  N3: LED2.cathode, R2.Pin_1
  N4: LED2.anode, ATMega328.A1, LED3.anode, LED6.cathode, LED7.cathode, LED8.anode, LED9.cathode, LED10.anode, LED1.anode
  N5: LED5.cathode, R5.Pin_1
  VCC: IR1.Vs, ATMega328.VCC, U1.output_voltage, HC-SR04_Sensor_1.VCC
  N6: IR1.Data, ATMega328.A0
  N7: R3.Pin_1, LED3.cathode
  N8: ATMega328.D7, HC-SR04_Sensor_1.ECHO
  N9: ATMega328.GND#21, HC-SR04_Sensor_1.GND
  N10: ATMega328.A2, SPKR1.pin2
  N11: LED4.cathode, R4.Pin_1
  N12: U1.input_voltage, J2.pin1
  N13: U1.GND, J2.pin2
  N14: LED6.anode, LED7.anode, LED9.anode
  N15: LED8.cathode, R7.Pin_1, R9.Pin_1
  N16: LED10.cathode, R11.Pin_1
  N17: R8.Pin_1, LED1.cathode

// code stored in the sketch: Arduino_Alarm.ino

const byte IR_SENSOR=A0;
const byte LIGHTS_PIN=A1;
const byte ALARM=A2;
const byte ACTIVATED_PIN=A3;
const byte DISTANCE_SENSORS[] = {7,7};

const float CMS_CONVERTER = 0.01723;
const byte TRIGGER_DISTANCE = 100;
unsigned long currentMillis;

long DISTANCE = 500;
bool ACTIVATED = false;
bool IR_PRESSED = false;
//Alarm.
unsigned long previousMillis = 0;
const long interval = 200;
int ALARM_STATE = LOW;

void setup() {
  Serial.begin(9600);
  pinMode(IR_SENSOR,INPUT);
  pinMode(LIGHTS_PIN,OUTPUT);
  pinMode(ACTIVATED_PIN,OUTPUT);
  pinMode(ALARM,OUTPUT);
}

void loop(){
  currentMillis = millis();
  readRemoteSignal();
  readDistanceSensor();
  //Serial.print(DISTANCE); Serial.println("cm");
  if(ACTIVATED){
    if(DISTANCE<=TRIGGER_DISTANCE){ soundAlarm(); }
    else{ stopAlarm(); }
  }
}
void readRemoteSignal(){
  if(digitalRead(IR_SENSOR)==LOW && !IR_PRESSED) {
	IR_PRESSED=true;
    ACTIVATED=!ACTIVATED;
    digitalWrite(ACTIVATED_PIN,ACTIVATED?HIGH:LOW);
    delay(500);
    Serial.print("ACTIVATED:"); Serial.println(ACTIVATED?"ON":"OFF");
  }else{ IR_PRESSED=false; }
}

void readDistanceSensor() {
  pinMode(DISTANCE_SENSORS[0], OUTPUT);  // Clear the trigger
  digitalWrite(DISTANCE_SENSORS[0], LOW);
  delayMicroseconds(2);
  // Sets the trigger pin to HIGH state for 10 microseconds
  digitalWrite(DISTANCE_SENSORS[0], HIGH);
  delayMicroseconds(10);
  digitalWrite(DISTANCE_SENSORS[0], LOW);
  pinMode(DISTANCE_SENSORS[1], INPUT);
  // Reads the echo pin, and returns the sound wave travel time in microseconds
  //return 0.01723 * pulseIn(DISTANCE_SENSORS[1], HIGH);
  DISTANCE = CMS_CONVERTER * pulseIn(DISTANCE_SENSORS[1], HIGH);
}

void soundAlarm(){
  if (currentMillis - previousMillis >= interval) {
    previousMillis = currentMillis;
    ALARM_STATE = ALARM_STATE==LOW? HIGH:LOW;
  	digitalWrite(LIGHTS_PIN,ALARM_STATE); 
    tone(ALARM, 1300, 100);
  }
  
}

void stopAlarm(){
  ALARM_STATE=LOW;
  digitalWrite(ALARM,LOW);
  digitalWrite(LIGHTS_PIN,LOW);
}
